// Logisim project adder.circ as structural Verilog: 4 circuits, main circuit main
module main (
  input  ADD_SUB,
  input  [7:0] A,
  input  [7:0] B,
  output [7:0] Output,
  output Carry_Borrow_prime
);

  wire Full_Adder_2_cout, Full_Adder_3_cout, Full_Adder_4_cout, Full_Adder_5_cout, Full_Adder_6_cout,
       Full_Adder_7_cout, Full_Adder_cout, xor_1_out, xor_2_out, xor_3_out, xor_4_out, xor_5_out, xor_6_out,
       xor_7_out, xor_8_out;

  xor xor_1 (xor_1_out, B[0], ADD_SUB);
  xor xor_2 (xor_2_out, B[1], ADD_SUB);
  xor xor_3 (xor_3_out, B[2], ADD_SUB);
  xor xor_4 (xor_4_out, B[3], ADD_SUB);
  xor xor_5 (xor_5_out, B[4], ADD_SUB);
  xor xor_6 (xor_6_out, B[5], ADD_SUB);
  xor xor_7 (xor_7_out, B[6], ADD_SUB);
  xor xor_8 (xor_8_out, B[7], ADD_SUB);
  Full_Adder Full_Adder (.cin(ADD_SUB), .A(A[0]), .B(xor_1_out), .sum(Output[0]), .cout(Full_Adder_cout));
  Full_Adder Full_Adder_2 (.cin(Full_Adder_cout), .A(A[1]), .B(xor_2_out), .sum(Output[1]), .cout(Full_Adder_2_cout));
  Full_Adder Full_Adder_3 (.cin(Full_Adder_2_cout), .A(A[2]), .B(xor_3_out), .sum(Output[2]), .cout(Full_Adder_3_cout));
  Full_Adder Full_Adder_4 (.cin(Full_Adder_3_cout), .A(A[3]), .B(xor_4_out), .sum(Output[3]), .cout(Full_Adder_4_cout));
  Full_Adder Full_Adder_5 (.cin(Full_Adder_4_cout), .A(A[4]), .B(xor_5_out), .sum(Output[4]), .cout(Full_Adder_5_cout));
  Full_Adder Full_Adder_6 (.cin(Full_Adder_5_cout), .A(A[5]), .B(xor_6_out), .sum(Output[5]), .cout(Full_Adder_6_cout));
  Full_Adder Full_Adder_7 (.cin(Full_Adder_6_cout), .A(A[6]), .B(xor_7_out), .sum(Output[6]), .cout(Full_Adder_7_cout));
  Full_Adder Full_Adder_8 (
    .cin(Full_Adder_7_cout), .A(A[7]), .B(xor_8_out), .sum(Output[7]), .cout(Carry_Borrow_prime));
endmodule

module Half_Adder (
  input  A,
  input  B,
  output sum,
  output cout
);

  xor xor_1 (sum, A, B);
  and and_1 (cout, A, B);
endmodule

module Full_Adder (
  input  cin,
  input  A,
  input  B,
  output sum,
  output cout
);

  wire Half_Adder_2_cout, Half_Adder_cout, Half_Adder_sum;

  Half_Adder Half_Adder (.A(A), .B(B), .sum(Half_Adder_sum), .cout(Half_Adder_cout));
  Half_Adder Half_Adder_2 (.A(cin), .B(Half_Adder_sum), .sum(sum), .cout(Half_Adder_2_cout));
  or or_1 (cout, Half_Adder_2_cout, Half_Adder_cout);
endmodule

module multiplier (
  input  [7:0] in_1
);

  Adder adder_1 ();  // open: a, b, out, cin, cout

  // Other names for the same wires on the sheet: B0 = in_1[0]
endmodule
