// Logisim project cpu.circ as structural Verilog: 7 circuits, main circuit main
module main (
  output [7:0] DataOut,
  output [3:0] _4_bit_opcode,
  output ADD,
  output SUB,
  output JMP,
  output AND,
  output OR,
  output MUL,
  output XOR,
  output MOV,
  output LOD,
  output STR,
  output NOT,
  output DIV,
  output HLT
);

  wire and_3_out, C1, C2, C3, C4, C5, C6, C7, Clk, Clk1, IMD, mem, not_1_out, not_2_out, or_1_out, or_2_out,
       Read, Reset, Write;
  wire [2:0] counter_1_counter, R1;
  wire [7:0] Address, ALUop, DIN, IMDVAL, multiplexer_1_out, multiplexer_2_out, multiplexer_3_out, PCA, PCA1,
       regfile_1_out_b, regfile_1_r1, regfile_1_r2;

  or or_1 (or_1_out, Reset, HLT);
  // Probe on counter_1_counter
  counter counter_1 (
    .Clk(Clk1), .Counter(counter_1_counter), .Clear(or_1_out), .C1(C1), .C2(C2), .C3(C3), .C4(C4), .C5(C5),
    .C6(C6), .C7(C7));
  or or_2 (or_2_out, Reset, HLT);
  PC pc_1 (.Offset(IMDVAL), .JMP(JMP), .Clock(Clk1), .Clear(or_2_out), .Enable(C7), .PCVal(PCA));
  // Probe on PCA
  Button button_1 (.out(Reset));
  Shift_Register High (
    .shift(1'b0), .clk(Clk1), .load(C1), .d0(DataOut[7]), .q0(IMD), .d1(DataOut[6]), .q1(_4_bit_opcode[3]),
    .d2(DataOut[5]), .q2(_4_bit_opcode[2]), .d3(DataOut[4]), .q3(_4_bit_opcode[1]), .d4(DataOut[3]),
    .q4(_4_bit_opcode[0]), .d5(DataOut[2]), .q5(R1[2]), .d6(DataOut[1]), .q6(R1[1]), .d7(DataOut[0]),
    .q7(R1[0]));  // open: in, out, clr
  Decoder #(.select(4), .enable("false")) decoder_1 (
    .out1(ADD), .out2(SUB), .out3(JMP), .out4(AND), .out5(OR), .out6(MUL), .out7(XOR), .out8(MOV),
    .out9(LOD), .out10(STR), .out11(NOT), .out12(DIV), .out15(HLT), .sel(_4_bit_opcode));  // open: out0, out13, out14
  // Probe on DIN
  Multiplexer #(.width(8), .enable("false")) multiplexer_1 (
    .in0(Address), .in1(IMDVAL), .out(multiplexer_1_out), .sel(mem));
  // Probe on multiplexer_1_out
  Shift_Register Low (
    .shift(1'b0), .clk(Clk1), .load(C2), .d0(DataOut[7]), .q0(IMDVAL[7]), .d1(DataOut[6]), .q1(IMDVAL[6]),
    .d2(DataOut[5]), .q2(IMDVAL[5]), .d3(DataOut[4]), .q3(IMDVAL[4]), .d4(DataOut[3]), .q4(IMDVAL[3]),
    .d5(DataOut[2]), .q5(IMDVAL[2]), .d6(DataOut[1]), .q6(IMDVAL[1]), .d7(DataOut[0]), .q7(IMDVAL[0]));  // open: in, out, clr
  // Probe on R1
  assign DataOut = Write ? DIN : 8'bz;  // Controlled_Buffer controlled_buffer_1
  RAM ram_1 (.addr(multiplexer_1_out), .data(DataOut), .sel(1'b1), .clk(Clk1), .ld(not_1_out), .clr(1'b0));
  not not_1 (not_1_out, Write);
  // Probe on IMDVAL
  // Probe on Write
  // Probe on IMDVAL[7:5]
  // Probe on regfile_1_r1
  // Probe on regfile_1_r2
  regfile regfile_1 (
    .Clock(Clk), .Add_A(R1), .Add_B(IMDVAL[7:5]), .R1(regfile_1_r1), .R2(regfile_1_r2), .Out_A(DIN),
    .Out_B(regfile_1_out_b), .In_A(multiplexer_2_out), .RF_Write(C5), .CLR(Reset));
  // Probe on DIN
  // Probe on multiplexer_3_out
  ALU alu_1 (
    .Operand_1(DIN), .Operand_2(multiplexer_3_out), ._4_bit_opcode(_4_bit_opcode), .ALU_Output(ALUop));  // open: NZ
  Multiplexer #(.width(8), .enable("false")) multiplexer_2 (
    .in0(ALUop), .in1(DataOut), .out(multiplexer_2_out), .sel(LOD));
  Multiplexer #(.width(8), .enable("false")) multiplexer_3 (
    .in0(regfile_1_out_b), .in1(IMDVAL), .out(multiplexer_3_out), .sel(IMD));
  // Probe on ALUop
  Clock clock_1 (.out(Clk));
  and and_1 (Write, C5, STR);
  and and_2 (Read, C4, LOD);
  not not_2 (not_2_out, HLT);
  Adder adder_1 (.a(PCA), .b(8'h1), .out(PCA1));  // open: cin, cout
  Multiplexer #(.select(2), .width(8), .enable("false")) multiplexer_4 (
    .in1(PCA1), .in2(PCA), .in3(IMDVAL), .out(Address), .sel({C1, C2}));  // open: in0
  and and_3 (and_3_out, Clk, not_2_out);
  or or_3 (mem, Write, Read);
  or or_4 (Clk1, and_3_out, Reset);

  // Other names for the same wires on the sheet: Load = LOD; MDR[7:0] = DataOut; R2[2:0] = IMDVAL[7:5]
endmodule

module ALU (
  input  [7:0] Operand_1,
  input  [7:0] Operand_2,
  input  [3:0] _4_bit_opcode,
  output [7:0] ALU_Output,
  output NZ
);

  wire AOF, SOF;
  wire [7:0] ADD, AND, DIV, MUL, NOT, OR, SUB, XOR;

  assign AND = Operand_1 & Operand_2;  // AND_Gate and_1, 8 bits wide
  assign OR = Operand_1 | Operand_2;  // OR_Gate or_1, 8 bits wide
  assign XOR = Operand_1 ^ Operand_2;  // XOR_Gate xor_1, 8 bits wide
  assign NOT = ~Operand_1;  // NOT_Gate not_1, 8 bits wide
  Adder adder_1 (.a(Operand_1), .b(Operand_2), .out(ADD), .cout(AOF));  // open: cin
  Subtractor subtractor_1 (.a(Operand_1), .b(Operand_2), .out(SUB), .bout(SOF));  // open: bin
  Multiplier multiplier_1 (.a(Operand_1), .b(Operand_2), .out(MUL));  // open: cin, cout
  Divider divider_1 (.a(Operand_1), .b(Operand_2), .out(DIV));  // open: upper, rem
  Multiplexer #(.select(4), .width(8), .enable("false")) multiplexer_1 (
    .in1(ADD), .in2(SUB), .in3(Operand_1), .in4(AND), .in5(OR), .in6(MUL), .in7(XOR), .in8(Operand_2),
    .in9(Operand_2), .in10(Operand_1), .in11(NOT), .in12(DIV), .out(ALU_Output), .sel(_4_bit_opcode));  // open: in0, in13, in14, in15
  or or_2 (NZ, ALU_Output[7], ALU_Output[6], ALU_Output[5], ALU_Output[4], ALU_Output[3], ALU_Output[2], ALU_Output[1], ALU_Output[0]);

  // Other names for the same wires on the sheet: _4_Bit_op_code[3:0] = _4_bit_opcode; B[7:0] = Operand_2;
  //   LOD[7:0] = Operand_2; MOV[7:0] = Operand_2; A[7:0] = Operand_1; JMP[7:0] = Operand_1; STR[7:0] = Operand_1
endmodule

module memory (
  input  [7:0] DataIN,
  input  [7:0] Address,
  input  Clock,
  input  Control,
  output [7:0] DataOut
);

  wire not_1_out;

  assign DataOut = Control ? DataIN : 8'bz;  // Controlled_Buffer controlled_buffer_1
  RAM ram_1 (.addr(Address), .data(DataOut), .sel(1'b1), .clk(Clock), .ld(not_1_out), .clr(1'b0));
  not not_1 (not_1_out, Control);
endmodule

module instruction_decoder (
  input  Clock,
  input  C1,
  input  C2,
  input  [7:0] Data,
  output [2:0] R1,
  output [2:0] R2,
  output [7:0] IMDVal,
  output [3:0] _4_bit_opcode,
  output ADD,
  output Immediate,
  output SUB,
  output JMP,
  output AND,
  output OR,
  output MUL,
  output XOR,
  output MOV,
  output LOD,
  output STR,
  output NOT,
  output DIV,
  output HLT
);

  Shift_Register High (
    .clk(Clock), .load(C1), .d0(Data[7]), .q0(Immediate), .d1(Data[6]), .q1(_4_bit_opcode[3]), .d2(Data[5]),
    .q2(_4_bit_opcode[2]), .d3(Data[4]), .q3(_4_bit_opcode[1]), .d4(Data[3]), .q4(_4_bit_opcode[0]),
    .d5(Data[2]), .q5(R1[2]), .d6(Data[1]), .q6(R1[1]), .d7(Data[0]), .q7(R1[0]));  // open: shift, in, out, clr
  Decoder #(.select(4), .enable("false")) decoder_1 (
    .out1(ADD), .out2(SUB), .out3(JMP), .out4(AND), .out5(OR), .out6(MUL), .out7(XOR), .out8(MOV),
    .out9(LOD), .out10(STR), .out11(NOT), .out12(DIV), .out15(HLT), .sel(_4_bit_opcode));  // open: out0, out13, out14
  Shift_Register Low (
    .clk(Clock), .load(C2), .d0(Data[7]), .q0(IMDVal[7]), .d1(Data[6]), .q1(IMDVal[6]), .d2(Data[5]),
    .q2(IMDVal[5]), .d3(Data[4]), .q3(IMDVal[4]), .d4(Data[3]), .q4(IMDVal[3]), .d5(Data[2]), .q5(IMDVal[2]),
    .d6(Data[1]), .q6(IMDVal[1]), .d7(Data[0]), .q7(IMDVal[0]));  // open: shift, in, out, clr

  assign R2 = IMDVal[7:5];
endmodule

module regfile (
  input  Clock,
  input  [2:0] Add_A,
  input  [2:0] Add_B,
  input  [7:0] In_A,
  input  RF_Write,
  input  CLR,
  output [7:0] R1,
  output [7:0] R2,
  output [7:0] Out_A,
  output [7:0] Out_B
);

  wire E1, E2, E3, E4, E5, E6;
  wire [7:0] C1, C2, C3, C4, C5, C6, R3, R4, R5, R6;

  Register u_R1 (.D(C1), .en(E1), .Q(R1), .clk(Clock), .clr(CLR));
  Register u_R3 (.D(C3), .en(E3), .Q(R3), .clk(Clock), .clr(CLR));
  Register u_R5 (.D(C5), .en(E5), .Q(R5), .clk(Clock), .clr(CLR));
  Multiplexer #(.select(3), .width(8), .enable("false")) multiplexer_1 (
    .in0(R1), .in1(R2), .in2(R3), .in3(R4), .in4(R5), .in5(R6), .out(Out_A), .sel(Add_A));  // open: in6, in7
  Register u_R2 (.D(C2), .en(E2), .Q(R2), .clk(Clock), .clr(CLR));
  Register u_R4 (.D(C4), .en(E4), .Q(R4), .clk(Clock), .clr(CLR));
  Register u_R6 (.D(C6), .en(E6), .Q(R6), .clk(Clock), .clr(CLR));
  Multiplexer #(.select(3), .width(8), .enable("false")) multiplexer_2 (
    .in0(R1), .in1(R2), .in2(R3), .in3(R4), .in4(R5), .in5(R6), .out(Out_B), .sel(Add_B));  // open: in6, in7
  Demultiplexer #(.select(3), .width(8)) demultiplexer_1 (
    .out0(C1), .out1(C2), .out2(C3), .out3(C4), .out4(C5), .out5(C6), .in(In_A), .sel(Add_A), .en(RF_Write));  // open: out6, out7
  Demultiplexer #(.select(3)) demultiplexer_2 (
    .out0(E1), .out1(E2), .out2(E3), .out3(E4), .out4(E5), .out5(E6), .in(1'b1), .sel(Add_A), .en(RF_Write));  // open: out6, out7

  // Other names for the same wires on the sheet: AddA[2:0] = Add_A; AddB[2:0] = Add_B; Clk = Clock
endmodule

module PC (
  input  [7:0] Offset,
  input  JMP,
  input  Enable,
  input  Clock,
  input  Clear,
  output [7:0] PCVal
);

  wire not_1_out;
  wire [7:0] adder_1_out, multiplexer_1_out;

  not not_1 (not_1_out, JMP);
  Multiplexer #(.width(8), .enable("false")) multiplexer_1 (
    .in0(Offset), .in1(adder_1_out), .out(multiplexer_1_out), .sel(not_1_out));
  Register PC (.D(multiplexer_1_out), .en(Enable), .Q(PCVal), .clk(Clock), .clr(Clear));
  Adder adder_1 (.a(PCVal), .b(8'h2), .out(adder_1_out));  // open: cin, cout
endmodule

// Counter
module counter (
  input  Clear,
  input  Clk,
  output [2:0] Counter,
  output C1,
  output C2,
  output C3,
  output C4,
  output C5,
  output C6,
  output C7
);

  wire multiplexer_1_out, not_1_out, not_2_out, not_3_out;

  Multiplexer #(.enable("false")) multiplexer_1 (.in0(1'b0), .in1(Clk), .out(multiplexer_1_out), .sel(1'b1));
  Counter #(.width(3), .max('h6)) counter_1 (
    .Q(Counter), .clk(multiplexer_1_out), .clr(Clear));  // open: load, D, count, carry
  not not_1 (not_1_out, Counter[0]);
  not not_2 (not_2_out, Counter[2]);
  not not_3 (not_3_out, Counter[1]);
  and and_1 (C1, not_1_out, not_3_out, not_2_out);
  and and_2 (C2, Counter[0], not_3_out, not_2_out);
  and and_3 (C3, not_2_out, Counter[1], not_1_out);
  and and_4 (C4, Counter[0], Counter[1], not_2_out);
  and and_5 (C5, not_1_out, not_3_out, Counter[2]);
  and and_6 (C6, Counter[0], not_3_out, Counter[2]);
  and and_7 (C7, Counter[2], Counter[1], not_1_out);
endmodule
