// Logisim project multiplier.circ as structural Verilog: 1 circuit, main circuit main
module main (
  input  [3:0] B,
  input  [3:0] A,
  output [7:0] out_3
);

  wire [2:0] and_14_out;
  wire [3:0] and_1_out, and_5_out, and_9_out;
  wire [3:1] adder_1_out, adder_2_out;
  wire [3:3] adder_1_cout, adder_2_cout;

  and and_1 (and_1_out[0], B[0], A[3]);
  and and_2 (and_1_out[1], B[1], A[3]);
  and and_3 (and_1_out[2], B[2], A[3]);
  and and_4 (and_1_out[3], B[3], A[3]);
  and and_5 (and_5_out[0], B[0], A[1]);
  and and_6 (and_5_out[1], B[1], A[1]);
  and and_7 (and_5_out[2], B[2], A[1]);
  and and_8 (and_5_out[3], B[3], A[1]);
  and and_9 (and_9_out[0], B[0], A[2]);
  and and_10 (and_9_out[1], B[1], A[2]);
  and and_11 (and_9_out[2], B[2], A[2]);
  and and_12 (and_9_out[3], B[3], A[2]);
  and and_13 (out_3[0], B[0], A[0]);
  and and_14 (and_14_out[0], B[1], A[0]);
  and and_15 (and_14_out[1], B[2], A[0]);
  and and_16 (and_14_out[2], B[3], A[0]);
  Adder #(.width(4)) adder_1 (
    .a({1'b0, and_14_out}), .b(and_5_out), .out({adder_1_out, out_3[1]}), .cout(adder_1_cout[3]));  // open: cin
  Adder #(.width(4)) adder_2 (
    .a({adder_1_cout[3], adder_1_out}), .b(and_9_out), .out({adder_2_out, out_3[2]}), .cout(adder_2_cout[3]));  // open: cin
  Adder #(.width(4)) adder_3 (
    .a({adder_2_cout[3], adder_2_out}), .b(and_1_out), .out(out_3[6:3]), .cout(out_3[7]));  // open: cin
endmodule
